// Logisim project 8bitCPU_t2.circ as structural Verilog: 4 circuits, main circuit main
module main (
  input  in_1,
  input  in_2,
  input  [2:0] in_3,
  input  in_4,
  input  in_5,
  input  in_6,
  input  in_7,
  input  CLK,
  input  [2:0] in_9,
  input  in_10,
  input  in_11,
  input  [2:0] in_12
);

  wire alu_1_subcout, alu_1_sumcout;
  wire [2:0] undriven;
  wire [7:0] alu_1_outalu, controlled_buffer_1_out, controlled_buffer_2_out, controlled_buffer_3_out,
       controlunit_1_outputsignals, counter_1_q, InstructionRegister_q, multiplexer_1_out, ram_1_dout,
       register_1_q, register_2_q, register_3_q, registerfile_1_outputdata;

  Counter counter_1 (
    .load(in_5), .count(controlunit_1_outputsignals[0]), .Q(counter_1_q), .clk(CLK));  // open: D, carry, up, clr
  Multiplexer #(.width(8)) multiplexer_1 (
    .in0({8{1'b1}}), .in1(counter_1_q), .out(multiplexer_1_out), .sel(controlunit_1_outputsignals[1]));
  RAM #(.\type ("nonvolatile")) ram_1 (
    .addr(register_1_q), .we(in_10), .oe(controlunit_1_outputsignals[3]), .clk(CLK),
    .din(controlled_buffer_1_out), .dout(ram_1_dout));
  Register register_1 (
    .D(multiplexer_1_out), .en(controlunit_1_outputsignals[2]), .clk(CLK), .Q(register_1_q));  // open: clr
  assign controlled_buffer_1_out = in_1 ? controlled_buffer_2_out : 8'bz;  // Controlled_Buffer controlled_buffer_1
  ControlUnit controlunit_1 (.CLK(CLK), .outputSignals(controlunit_1_outputsignals));
  Register register_2 (.D(ram_1_dout), .en(controlunit_1_outputsignals[4]), .clk(CLK), .Q(register_2_q));  // open: clr
  assign controlled_buffer_2_out = controlunit_1_outputsignals[5] ? register_2_q : 8'bz;  // Controlled_Buffer controlled_buffer_2
  Register InstructionRegister (
    .D(controlled_buffer_2_out), .en(in_2), .clk(CLK), .Q(InstructionRegister_q));  // open: clr
  RegisterFile registerfile_1 (
    .CLK(CLK), .bitSel(in_9), .writeEnb(in_11), .outBitSel(in_12), .outputData(registerfile_1_outputdata));  // open: inputData
  assign controlled_buffer_3_out = in_7 ? registerfile_1_outputdata : 8'bz;  // Controlled_Buffer controlled_buffer_3
  Register register_3 (.D(controlled_buffer_3_out), .en(in_4), .clk(CLK), .Q(register_3_q));  // open: clr
  ALU alu_1 (
    .A(register_3_q), .B(registerfile_1_outputdata), .shiftAmount(undriven), .aluMux(in_3), .aluMuxEnb(in_6),
    .outALU(alu_1_outalu), .sumCout(alu_1_sumcout), .subCout(alu_1_subcout));
endmodule

module ALU (
  input  [7:0] A,
  input  [7:0] B,
  input  [2:0] shiftAmount,
  input  [2:0] aluMux,
  input  aluMuxEnb,
  output [7:0] outALU,
  output sumCout,
  output subCout
);

  wire [7:0] adder_1_out, and_1_out, not_1_out, or_1_out, shifter_1_out, shifter_2_out, subtractor_1_out,
       xor_1_out;

  Adder adder_1 (.a(A), .b(B), .out(adder_1_out), .cout(sumCout));  // open: cin
  Subtractor subtractor_1 (.a(A), .b(B), .out(subtractor_1_out), .bout(subCout));  // open: bin
  Shifter shifter_1 (.in(A), .\dist (shiftAmount), .out(shifter_1_out));
  Shifter #(.shift("lr")) shifter_2 (.in(A), .\dist (shiftAmount), .out(shifter_2_out));
  assign not_1_out = ~A;  // NOT_Gate not_1, 8 bits wide
  assign and_1_out = A & B;  // AND_Gate and_1, 8 bits wide
  assign or_1_out = B | B;  // OR_Gate or_1, 8 bits wide
  assign xor_1_out = A ^ B;  // XOR_Gate xor_1, 8 bits wide
  Multiplexer #(.enable("true"), .select(3), .width(8)) multiplexer_1 (
    .in0(adder_1_out), .in1(subtractor_1_out), .in2(shifter_1_out), .in3(shifter_2_out), .in4(and_1_out),
    .in5(or_1_out), .in6(not_1_out), .in7(xor_1_out), .out(outALU), .sel(aluMux), .en(aluMuxEnb));
endmodule

module RegisterFile (
  input  CLK,
  input  [7:0] inputData,
  input  [2:0] bitSel,
  input  writeEnb,
  input  [2:0] outBitSel,
  output [7:0] outputData
);

  wire demultiplexer_1_out0, demultiplexer_1_out1, demultiplexer_1_out2, demultiplexer_1_out3,
       demultiplexer_1_out4, demultiplexer_1_out5, demultiplexer_1_out6, demultiplexer_1_out7, undriven,
       undriven_2, undriven_3, undriven_4, undriven_5, undriven_6, undriven_7, undriven_8;
  wire [7:0] demultiplexer_2_out0, demultiplexer_2_out1, demultiplexer_2_out2, demultiplexer_2_out3,
       demultiplexer_2_out4, demultiplexer_2_out5, demultiplexer_2_out6, demultiplexer_2_out7, register_1_q,
       register_2_q, register_3_q, register_4_q, register_5_q, register_6_q, register_7_q, register_8_q;

  Demultiplexer #(.select(3)) demultiplexer_1 (
    .out0(demultiplexer_1_out0), .out1(demultiplexer_1_out1), .out2(demultiplexer_1_out2),
    .out3(demultiplexer_1_out3), .out4(demultiplexer_1_out4), .out5(demultiplexer_1_out5),
    .out6(demultiplexer_1_out6), .out7(demultiplexer_1_out7), .in(writeEnb), .sel(bitSel));
  Demultiplexer #(.select(3), .width(8)) demultiplexer_2 (
    .out0(demultiplexer_2_out0), .out1(demultiplexer_2_out1), .out2(demultiplexer_2_out2),
    .out3(demultiplexer_2_out3), .out4(demultiplexer_2_out4), .out5(demultiplexer_2_out5),
    .out6(demultiplexer_2_out6), .out7(demultiplexer_2_out7), .in(inputData), .sel(bitSel));
  Register register_1 (
    .D(demultiplexer_2_out0), .en(demultiplexer_1_out0), .clk(CLK), .Q(register_1_q), .clr(undriven));
  Register register_2 (
    .D(demultiplexer_2_out1), .en(demultiplexer_1_out1), .clk(CLK), .Q(register_2_q), .clr(undriven_2));
  Register register_3 (
    .D(demultiplexer_2_out2), .en(demultiplexer_1_out2), .clk(CLK), .Q(register_3_q), .clr(undriven_3));
  Register register_4 (
    .D(demultiplexer_2_out3), .en(demultiplexer_1_out3), .clk(CLK), .Q(register_4_q), .clr(undriven_4));
  Register register_5 (
    .D(demultiplexer_2_out4), .en(demultiplexer_1_out4), .clk(CLK), .Q(register_5_q), .clr(undriven_5));
  Register register_6 (
    .D(demultiplexer_2_out5), .en(demultiplexer_1_out5), .clk(CLK), .Q(register_6_q), .clr(undriven_6));
  Register register_7 (
    .D(demultiplexer_2_out6), .en(demultiplexer_1_out6), .clk(CLK), .Q(register_7_q), .clr(undriven_7));
  Register register_8 (
    .D(demultiplexer_2_out7), .en(demultiplexer_1_out7), .clk(CLK), .Q(register_8_q), .clr(undriven_8));
  Multiplexer #(.select(3), .width(8)) multiplexer_1 (
    .in0(register_1_q), .in1(register_2_q), .in2(register_3_q), .in3(register_4_q), .in4(register_5_q),
    .in5(register_6_q), .in6(register_7_q), .in7(register_8_q), .out(outputData), .sel(outBitSel));
endmodule

module ControlUnit (
  input  CLK,
  output [7:0] outputSignals
);

  wire demultiplexer_1_out0, demultiplexer_1_out1, demultiplexer_1_out2;
  wire [2:0] counter_1_q;

  Counter #(.max('h7), .width(3)) counter_1 (.count(CLK), .Q(counter_1_q), .clk(CLK));  // open: load, D, carry, up, clr
  buf PC_enb (outputSignals[0], demultiplexer_1_out0);  // OR_Gate
  buf MUX_enb (outputSignals[1], demultiplexer_1_out0);  // OR_Gate
  buf MAR (outputSignals[2], demultiplexer_1_out0);  // OR_Gate
  buf RAM_out (outputSignals[3], demultiplexer_1_out1);  // OR_Gate
  buf MDR_WE (outputSignals[4], demultiplexer_1_out1);  // OR_Gate
  buf MDR_out (outputSignals[5], demultiplexer_1_out1);  // OR_Gate
  Demultiplexer #(.select(3)) demultiplexer_1 (
    .out0(demultiplexer_1_out0), .out1(demultiplexer_1_out1), .out2(demultiplexer_1_out2), .in(1'b1),
    .sel(counter_1_q));  // open: out3, out4, out5, out6, out7
endmodule
