// Logisim project 8bitCPU_t2.circ as structural Verilog: 5 circuits, main circuit main
module main (
  input  in_1,
  input  [2:0] in_2,
  input  in_3,
  input  in_4,
  input  in_5,
  input  in_6,
  input  CLK,
  input  in_8,
  input  in_9
);

  wire alu_1_subcout, alu_1_sumcout, CLK_t;
  wire [2:0] controlled_buffer_3_out, controlunit_1_posta, undriven;
  wire [5:0] controlunit_1_outlefts, controlunit_1_outrights;
  wire [7:0] alu_1_outalu, controlled_buffer_1_out, controlled_buffer_2_out, controlled_buffer_4_out,
       counter_1_q, InstructionRegister_q, multiplexer_1_out, ram_1_dout, register_1_q, register_2_q,
       register_3_q, registerfile_1_outputdata;

  Clock clock_1 (.out(CLK_t));
  Counter counter_1 (
    .load(in_4), .count(controlunit_1_outlefts[0]), .Q(counter_1_q), .clk(CLK_t));  // open: D, carry, up, clr
  Multiplexer #(.width(8)) multiplexer_1 (
    .in0({8{1'b1}}), .in1(counter_1_q), .out(multiplexer_1_out), .sel(controlunit_1_outlefts[1]));
  RAM #(.trigger("falling"), .\type ("nonvolatile")) ram_1 (
    .addr(register_1_q), .we(in_8), .oe(controlunit_1_outlefts[3]), .clk(CLK_t),
    .din(controlled_buffer_1_out), .dout(ram_1_dout));
  Register register_1 (
    .D(multiplexer_1_out), .en(controlunit_1_outlefts[2]), .clk(CLK_t), .Q(register_1_q));  // open: clr
  assign controlled_buffer_1_out = in_1 ? controlled_buffer_2_out : 8'bz;  // Controlled_Buffer controlled_buffer_1
  ControlUnit controlunit_1 (
    .regAdr_A(controlled_buffer_2_out), .opcode(InstructionRegister_q), .CLK(CLK_t),
    .posta(controlunit_1_posta), .outLeftS(controlunit_1_outlefts), .outRightS(controlunit_1_outrights));
  Register register_2 (.D(ram_1_dout), .en(controlunit_1_outlefts[4]), .clk(CLK_t), .Q(register_2_q));  // open: clr
  assign controlled_buffer_2_out = controlunit_1_outlefts[5] ? register_2_q : 8'bz;  // Controlled_Buffer controlled_buffer_2
  Controlled_Buffer #(.width(3)) controlled_buffer_3 (.out(controlled_buffer_3_out), .en(in_9));  // open: in
  Register InstructionRegister (
    .D(controlled_buffer_2_out), .en(controlunit_1_outrights[0]), .clk(CLK_t), .Q(InstructionRegister_q));  // open: clr
  RegisterFile registerfile_1 (
    .CLK(CLK_t), .inputData(controlled_buffer_2_out), .inputSel(controlunit_1_posta),
    .writeEnb(controlunit_1_outrights[1]), .outBitSel(controlled_buffer_3_out),
    .outputData(registerfile_1_outputdata));
  Register register_3 (.D(controlled_buffer_4_out), .en(in_3), .clk(CLK_t), .Q(register_3_q));  // open: clr
  assign controlled_buffer_4_out = in_6 ? registerfile_1_outputdata : 8'bz;  // Controlled_Buffer controlled_buffer_4
  ALU alu_1 (
    .A(register_3_q), .B(registerfile_1_outputdata), .shiftAmount(undriven), .aluMux(in_2), .aluMuxEnb(in_5),
    .outALU(alu_1_outalu), .sumCout(alu_1_sumcout), .subCout(alu_1_subcout));
endmodule

module ALU (
  input  [7:0] A,
  input  [7:0] B,
  input  [2:0] shiftAmount,
  input  [2:0] aluMux,
  input  aluMuxEnb,
  output [7:0] outALU,
  output sumCout,
  output subCout
);

  wire [7:0] adder_1_out, and_1_out, not_1_out, or_1_out, shifter_1_out, shifter_2_out, subtractor_1_out,
       xor_1_out;

  Adder adder_1 (.a(A), .b(B), .out(adder_1_out), .cout(sumCout));  // open: cin
  Subtractor subtractor_1 (.a(A), .b(B), .out(subtractor_1_out), .bout(subCout));  // open: bin
  Shifter shifter_1 (.in(A), .\dist (shiftAmount), .out(shifter_1_out));
  Shifter #(.shift("lr")) shifter_2 (.in(A), .\dist (shiftAmount), .out(shifter_2_out));
  assign not_1_out = ~A;  // NOT_Gate not_1, 8 bits wide
  assign and_1_out = A & B;  // AND_Gate and_1, 8 bits wide
  assign or_1_out = B | B;  // OR_Gate or_1, 8 bits wide
  assign xor_1_out = A ^ B;  // XOR_Gate xor_1, 8 bits wide
  Multiplexer #(.enable("true"), .select(3), .width(8)) multiplexer_1 (
    .in0(adder_1_out), .in1(subtractor_1_out), .in2(shifter_1_out), .in3(shifter_2_out), .in4(and_1_out),
    .in5(or_1_out), .in6(not_1_out), .in7(xor_1_out), .out(outALU), .sel(aluMux), .en(aluMuxEnb));
endmodule

module RegisterFile (
  input  CLK,
  input  [7:0] inputData,
  input  [2:0] inputSel,
  input  writeEnb,
  input  [2:0] outBitSel,
  output [7:0] outputData
);

  wire demultiplexer_1_out0, demultiplexer_1_out1, demultiplexer_1_out2, demultiplexer_1_out3,
       demultiplexer_1_out4, demultiplexer_1_out5, demultiplexer_1_out6, demultiplexer_1_out7, undriven,
       undriven_2, undriven_3, undriven_4, undriven_5, undriven_6, undriven_7, undriven_8;
  wire [7:0] demultiplexer_2_out0, demultiplexer_2_out1, demultiplexer_2_out2, demultiplexer_2_out3,
       demultiplexer_2_out4, demultiplexer_2_out5, demultiplexer_2_out6, demultiplexer_2_out7, register_1_q,
       register_2_q, register_3_q, register_4_q, register_5_q, register_6_q, register_7_q, register_8_q;

  Demultiplexer #(.select(3)) demultiplexer_1 (
    .out0(demultiplexer_1_out0), .out1(demultiplexer_1_out1), .out2(demultiplexer_1_out2),
    .out3(demultiplexer_1_out3), .out4(demultiplexer_1_out4), .out5(demultiplexer_1_out5),
    .out6(demultiplexer_1_out6), .out7(demultiplexer_1_out7), .in(writeEnb), .sel(inputSel));
  Demultiplexer #(.select(3), .width(8)) demultiplexer_2 (
    .out0(demultiplexer_2_out0), .out1(demultiplexer_2_out1), .out2(demultiplexer_2_out2),
    .out3(demultiplexer_2_out3), .out4(demultiplexer_2_out4), .out5(demultiplexer_2_out5),
    .out6(demultiplexer_2_out6), .out7(demultiplexer_2_out7), .in(inputData), .sel(inputSel));
  Register register_1 (
    .D(demultiplexer_2_out0), .en(demultiplexer_1_out0), .clk(CLK), .Q(register_1_q), .clr(undriven));
  Register register_2 (
    .D(demultiplexer_2_out1), .en(demultiplexer_1_out1), .clk(CLK), .Q(register_2_q), .clr(undriven_2));
  Register register_3 (
    .D(demultiplexer_2_out2), .en(demultiplexer_1_out2), .clk(CLK), .Q(register_3_q), .clr(undriven_3));
  Register register_4 (
    .D(demultiplexer_2_out3), .en(demultiplexer_1_out3), .clk(CLK), .Q(register_4_q), .clr(undriven_4));
  Register register_5 (
    .D(demultiplexer_2_out4), .en(demultiplexer_1_out4), .clk(CLK), .Q(register_5_q), .clr(undriven_5));
  Register register_6 (
    .D(demultiplexer_2_out5), .en(demultiplexer_1_out5), .clk(CLK), .Q(register_6_q), .clr(undriven_6));
  Register register_7 (
    .D(demultiplexer_2_out6), .en(demultiplexer_1_out6), .clk(CLK), .Q(register_7_q), .clr(undriven_7));
  Register register_8 (
    .D(demultiplexer_2_out7), .en(demultiplexer_1_out7), .clk(CLK), .Q(register_8_q), .clr(undriven_8));
  Multiplexer #(.select(3), .width(8)) multiplexer_1 (
    .in0(register_1_q), .in1(register_2_q), .in2(register_3_q), .in3(register_4_q), .in4(register_5_q),
    .in5(register_6_q), .in6(register_7_q), .in7(register_8_q), .out(outputData), .sel(outBitSel));
endmodule

module ControlUnit (
  input  [7:0] regAdr_A,
  input  [7:0] opcode,
  input  CLK,
  output [2:0] posta,
  output [5:0] outLeftS,
  output [5:0] outRightS
);

  wire and_1_out, and_2_out, and_4_out, decoder_1_out0, decoder_1_out1, decoder_1_out2, decoder_1_out3,
       decoder_1_out4, decoder_1_out5, decoder_1_out6, decoder_1_out7, decoder_1_out8, opLOAD, postaA_out,
       postaA_we, postaB_we;
  wire [2:0] postaA_q, postaB_q;
  wire [3:0] counter_1_q;

  OpcodeDecoder opcodedecoder_1 (
    .in_1(opcode), .op_LOAD(opLOAD));  // open: op_ADD, op_SUB, op_SHL, op_SHR, op_AND, op_OR, op_NOT, op_XOR, STR, MOV
  Counter #(.max('hf), .width(4)) counter_1 (.count(CLK), .Q(counter_1_q), .clk(CLK));  // open: load, D, carry, up, clr
  or PC_enb (outLeftS[0], decoder_1_out0, and_2_out, and_1_out);
  or MUX_enb (outLeftS[1], decoder_1_out0, and_2_out, and_1_out);
  or MAR (outLeftS[2], and_2_out, decoder_1_out0, and_1_out);
  or RAM_out (outLeftS[3], decoder_1_out1, and_2_out, and_4_out);
  or MDR_WE (outLeftS[4], and_4_out, decoder_1_out1, and_2_out);
  or MDR_out (outLeftS[5], decoder_1_out2, postaA_we, postaA_out);
  buf Instruction_WE (outRightS[0], decoder_1_out2);  // OR_Gate
  buf RegFile_WE (outRightS[1], postaA_out);  // OR_Gate
  Register #(.width(3)) postaA (.D(regAdr_A[2:0]), .en(postaA_we), .clk(CLK), .Q(postaA_q));  // open: clr
  Register #(.width(3)) postaB (.D(regAdr_A[5:3]), .en(postaB_we), .clk(CLK), .Q(postaB_q));  // open: clr
  assign posta = postaA_out ? postaA_q : 3'bz;  // Controlled_Buffer controlled_buffer_1
  assign posta = 1'b0 ? postaB_q : 3'bz;  // Controlled_Buffer controlled_buffer_2
  Decoder #(.enable("false"), .select(4)) decoder_1 (
    .out0(decoder_1_out0), .out1(decoder_1_out1), .out2(decoder_1_out2), .out3(decoder_1_out3),
    .out4(decoder_1_out4), .out5(decoder_1_out5), .out6(decoder_1_out6), .out7(decoder_1_out7),
    .out8(decoder_1_out8), .sel(counter_1_q));  // open: out9, out10, out11, out12, out13, out14, out15
  and and_1 (and_1_out, opLOAD, decoder_1_out3);
  and and_2 (and_2_out, decoder_1_out4, opLOAD);
  and and_3 (postaA_we, opLOAD, decoder_1_out5);
  and and_4 (and_4_out, opLOAD, decoder_1_out6);
  and and_5 (postaA_out, opLOAD, decoder_1_out7);
endmodule

module OpcodeDecoder (
  input  [7:0] in_1,
  output op_ADD,
  output op_SUB,
  output op_SHL,
  output op_SHR,
  output op_AND,
  output op_OR,
  output op_NOT,
  output op_XOR,
  output op_LOAD,
  output STR,
  output MOV
);

  Comparator comparator_1 (.a(in_1), .b(8'h8), .eq(op_ADD));  // open: gt, lt
  Comparator comparator_2 (.a(in_1), .b(8'h9), .eq(op_SUB));  // open: gt, lt
  Comparator comparator_3 (.a(in_1), .b(8'ha), .eq(op_SHL));  // open: gt, lt
  Comparator comparator_4 (.a(in_1), .b(8'hb), .eq(op_SHR));  // open: gt, lt
  Comparator comparator_5 (.a(in_1), .b(8'hc), .eq(op_AND));  // open: gt, lt
  Comparator comparator_6 (.a(in_1), .b(8'hd), .eq(op_OR));  // open: gt, lt
  Comparator comparator_7 (.a(in_1), .b(8'he), .eq(op_NOT));  // open: gt, lt
  Comparator comparator_8 (.a(in_1), .b(8'hf), .eq(op_XOR));  // open: gt, lt
  Comparator comparator_9 (.a(in_1), .b(8'h1), .eq(op_LOAD));  // open: gt, lt
  Comparator comparator_10 (.a(in_1), .b(8'h3), .eq(STR));  // open: gt, lt
  Comparator comparator_11 (.a(in_1), .b(8'h4), .eq(MOV));  // open: gt, lt
endmodule
